# Fritzing sketch regulator (saved by Fritzing 0.9.3b)
breadboards: 1

parts:
  R1 = Resistor [tolerance=±5% resistance=100k package=THT]
  R2 = Resistor [tolerance=±5% resistance=220 package=THT]
  C1 = Ceramic Capacitor [capacitance=10pF voltage=20V package="100 mil [THT, multilayer]"]
  C2 = Electrolytic Capacitor [capacitance=10µF package="100 mil [THT, electrolytic]"]
  U1 = Voltage Regulator - 5V [part_number=L7808 package="TO220 [THT]"]
  D1 = Rectifier Diode [part_number=1N4007 package="300 mil [THT]"]
  J2 = female pin header, 1 pin [form="♀ (female)"]
  J3 = female pin header, 1 pin [form="♀ (female)"]
  J4 = female pin header, 1 pin [form="♀ (female)"]
  J5 = female pin header, 1 pin [form="♀ (female)"]
  Mod1 = generic-ac-power-supply [package=THT]
  Part3 = Lilypad Battery Connect
  U2 = mystery part, 3 pins [chip_label=PVQ13]
  J1 = female pin header, 4 pins [form="♀ (female)"]
  U3 = mystery part, 3 pins [chip_label=PFM510]
  C3 = Electrolytic Capacitor [capacitance=10µF package="100 mil [THT, electrolytic]"]
  Q4 = NPN-Transistor [part_number=2N3904 package="TO92 [THT]"]
  Q6 = Basic FET N-Channel [part_number=IRFZ44N package="TO220 [THT]"]
  Part4 = Arduino Nano (Rev3.0)

nets:
  N1: R1.Pin_0, Part4.D6
  N2: R1.Pin_1, Q4.C, Q6.gate
  N3: R2.Pin_0, Q4.B, Q6.source
  GND: R2.Pin_1, C1.1, C2.+, U1.GND, J4.pin1, Mod1.pin4, J1.pin4, U3.pin3, C3.+, Q4.E, Part4.GND
  N4: C1.0, C2.-, U1.input_voltage, D1.anode, J2.pin1, J3.pin1, Mod1.pin3, U2.pin1, J1.pin2, U3.pin2
  N5: U1.L7808, C3.-, Part4.VIN
  N6: D1.cathode, J5.pin1, U2.pin3, Q6.drain
  N7: Mod1.pin1, Part3.-
  N8: Mod1.pin2, Part3.+
  N9: J1.pin1, U3.pin1, Part4.A0

notes:
  240V AC power supply
  PMF510 Flow sensor
  PVQ13 Solenoid Valve

custom parts:
  Voltage Regulator - 5V: 5V DC Voltage Regulator
  generic-ac-power-supply: Generic ac power supply module. Use as is, or customize the svgs to fit your particular device (as they are all different.) Provides AC input and single DC output. This is variant 2, with pcb modified to match the url for a specific device.
